// Logisim project part1.circ as structural Verilog: 2 circuits, main circuit main
module main (
  input  in_1,
  input  A,
  input  in_3,
  input  in_4,
  input  in_5,
  input  in_6,
  input  in_7,
  input  in_8,
  input  in_9,
  input  B,
  input  in_11,
  input  in_12,
  input  in_13,
  input  in_14,
  input  in_15,
  input  in_16,
  input  in_17,
  output out_18,
  output out_19,
  output out_20,
  output out_21,
  output out_22,
  output out_23,
  output out_24,
  output out_25
);

  wire ods3_2_cout, ods3_3_cout, ods3_4_cout, ods3_5_cout, ods3_6_cout, ods3_7_cout, ods3_8_cout;

  ODS3 ods3_1 (.A(A), .B(B), .cin(ods3_2_cout), .sum(out_18));  // open: cout
  ODS3 ods3_2 (.A(in_3), .B(in_11), .cin(ods3_3_cout), .sum(out_19), .cout(ods3_2_cout));
  ODS3 ods3_3 (.A(in_4), .B(in_12), .cin(ods3_4_cout), .sum(out_20), .cout(ods3_3_cout));
  ODS3 ods3_4 (.A(in_5), .B(in_13), .cin(ods3_5_cout), .sum(out_21), .cout(ods3_4_cout));
  ODS3 ods3_5 (.A(in_6), .B(in_14), .cin(ods3_6_cout), .sum(out_22), .cout(ods3_5_cout));
  ODS3 ods3_6 (.A(in_7), .B(in_15), .cin(ods3_7_cout), .sum(out_23), .cout(ods3_6_cout));
  ODS3 ods3_7 (.A(in_8), .B(in_16), .cin(ods3_8_cout), .sum(out_24), .cout(ods3_7_cout));
  ODS3 ods3_8 (.A(in_9), .B(in_17), .cin(in_1), .sum(out_25), .cout(ods3_8_cout));
endmodule

module ODS3 (
  input  A,
  input  B,
  input  cin,
  output sum,
  output cout
);

  wire and_1_out, and_2_out, and_3_out, and_4_out, and_5_out, and_6_out, and_7_out, notA_out, notB_out,
       notCIN_out;

  not notA (notA_out, A);
  not notB (notB_out, B);
  not notCIN (notCIN_out, cin);
  and and_1 (and_1_out, notA_out, notB_out, cin);
  and and_2 (and_2_out, notA_out, notCIN_out, B);
  and and_3 (and_3_out, notB_out, notCIN_out, A);
  and and_4 (and_4_out, A, B, cin);
  and and_5 (and_5_out, A, B);
  and and_6 (and_6_out, A, cin);
  and and_7 (and_7_out, B, cin);
  or or_1 (sum, and_1_out, and_2_out, and_3_out, and_4_out);
  or or_2 (cout, and_5_out, and_6_out, and_7_out);
endmodule
