// Logisim project part3.circ as structural Verilog: 1 circuit, main circuit main
module main (
  input  v,
  output out_2,
  output out_3,
  output out_4
);

  wire and_1_out, and_2_out, clock_1_out, q1_qn, q2_qn;

  Clock clock_1 (.out(clock_1_out));
  T_Flip_Flop q3 (.T(and_2_out), .clk(clock_1_out), .Q(out_2));  // open: Qn, reset, preset
  T_Flip_Flop q2 (.T(and_1_out), .clk(clock_1_out), .Q(out_3), .Qn(q2_qn));  // open: reset, preset
  T_Flip_Flop q1 (.T(v), .clk(clock_1_out), .Q(out_4), .Qn(q1_qn));  // open: reset, preset
  and and_1 (and_1_out, v, q1_qn);
  and and_2 (and_2_out, q1_qn, v, q2_qn);
endmodule
